// Logisim project CPU_IO_edit.circ as structural Verilog: 12 circuits, main circuit main
module main (
);

  wire clock_1_out, d_ff_1_q, Execute_1_bch, Memory_1_write, not_1_out, Reset_out,
       SimRAM_1_illegal_memory_access;
  wire [3:0] Decode_1_dste, Decode_1_dstm, Decode_1_srca, Decode_1_srcb, Fetch_1_icd, Fetch_1_ifn,
       Fetch_1_ra, Fetch_1_rb, multiplexer_1_out;
  wire [15:0] SimRAM_1_second_word;
  wire [63:0] Execute_1_vale, Fetch_1_valc, Fetch_1_valp, Memory_1_address, Memory_1_data, PCUpdate_1_nextpc,
       Program_Counter_q, Registers_1_eax, Registers_1_ebp, Registers_1_ebx, Registers_1_ecx,
       Registers_1_edi, Registers_1_edx, Registers_1_esi, Registers_1_esp, Registers_1_r9, Registers_1_r10,
       Registers_1_r11, Registers_1_r12, Registers_1_r13, Registers_1_r14, Registers_1_rto, Registers_1_vala,
       Registers_1_valb, SimRAM_1_first_word;

  Button Reset (.out(Reset_out));
  Clock clock_1 (.out(clock_1_out));
  D_Flip_Flop d_ff_1 (.clk(clock_1_out), .D(not_1_out), .Q(d_ff_1_q), .preset(1'b0), .reset(Reset_out));  // open: Qn
  not not_1 (not_1_out, d_ff_1_q);
  Register #(.width(64)) Program_Counter (
    .D(PCUpdate_1_nextpc), .en(d_ff_1_q), .clk(clock_1_out), .Q(Program_Counter_q), .clr(Reset_out));
  LED LED_1 (.in(SimRAM_1_illegal_memory_access));
  SimRAM SimRAM_1 (
    .Write(Memory_1_write), .Data_from_Memory_Stage(Memory_1_data),
    .Addr_from_Memory_Stage(Memory_1_address), .Clock(clock_1_out), .Substep_Number(d_ff_1_q),
    .Program_Counter(PCUpdate_1_nextpc), .Illegal_Memory_Access(SimRAM_1_illegal_memory_access),
    .First_Word(SimRAM_1_first_word), .Second_Word(SimRAM_1_second_word));
  // Probe on Fetch_1_icd
  // Probe on Fetch_1_ifn
  PCUpdate PCUpdate_1 (
    .valM(SimRAM_1_first_word), .iCd(Fetch_1_icd), .valP(Fetch_1_valp), .valC(Fetch_1_valc),
    .bch(Execute_1_bch), .Substep(d_ff_1_q), .Clock(clock_1_out), .nextPC(PCUpdate_1_nextpc));
  Memory Memory_1 (
    .valE(Execute_1_vale), .valA(Registers_1_vala), .valP(Fetch_1_valp), .iCd(Fetch_1_icd),
    .Write(Memory_1_write), .Data(Memory_1_data), .Address(Memory_1_address));
  Execute Execute_1 (
    .valA(Registers_1_vala), .valB(Registers_1_valb), .valC(Fetch_1_valc), .Clock(clock_1_out),
    .Reset(Reset_out), .iCd(Fetch_1_icd), .iFn(Fetch_1_ifn), .Step(d_ff_1_q), .valE(Execute_1_vale),
    .Bch(Execute_1_bch));
  Decode Decode_1 (
    .rA(Fetch_1_ra), .rB(Fetch_1_rb), .iCd(Fetch_1_icd), .srcA(Decode_1_srca), .srcB(Decode_1_srcb),
    .dstE(Decode_1_dste), .dstM(Decode_1_dstm));
  Fetch Fetch_1 (
    .First_Word(SimRAM_1_first_word), .Second_Word(SimRAM_1_second_word), .Substep(d_ff_1_q),
    .Program_Counter(Program_Counter_q), .Clock(clock_1_out), .iCd(Fetch_1_icd), .IFn(Fetch_1_ifn),
    .valP(Fetch_1_valp), .rA(Fetch_1_ra), .rB(Fetch_1_rb), .valC(Fetch_1_valc));
  // Probe on Fetch_1_ra
  // Probe on Fetch_1_rb
  // Probe on Decode_1_srca
  // Probe on Decode_1_srcb
  Multiplexer #(.width(4)) multiplexer_1 (
    .in0(4'b1111), .in1(Decode_1_dste), .out(multiplexer_1_out), .sel(Execute_1_bch));
  Registers Registers_1 (
    .dstE(multiplexer_1_out), .dstM(Decode_1_dstm), .valE(Execute_1_vale), .valM(SimRAM_1_first_word),
    .srcA(Decode_1_srca), .srcB(Decode_1_srcb), .Clock(clock_1_out), .Reset(Reset_out), .Substep(d_ff_1_q),
    .eax(Registers_1_eax), .ecx(Registers_1_ecx), .edx(Registers_1_edx), .ebx(Registers_1_ebx),
    .esp(Registers_1_esp), .ebp(Registers_1_ebp), .esi(Registers_1_esi), .edi(Registers_1_edi),
    .valA(Registers_1_vala), .valB(Registers_1_valb), .rto(Registers_1_rto), .r9(Registers_1_r9),
    .r10(Registers_1_r10), .r11(Registers_1_r11), .r12(Registers_1_r12), .r13(Registers_1_r13),
    .r14(Registers_1_r14));
  // Probe on Execute_1_bch
  // Probe on SimRAM_1_first_word
  // Probe on Registers_1_valb
  // Probe on Registers_1_vala
  // Probe on Execute_1_vale
  // Probe on Registers_1_eax
  // Probe on Registers_1_ecx
  // Probe on Registers_1_edx
  // Probe on Registers_1_ebx
  // Probe on Registers_1_esp
  // Probe on Registers_1_ebp
  // Probe on Registers_1_esi
  // Probe on Registers_1_edi
  // Probe on Registers_1_rto
  // Probe on Registers_1_r9
  // Probe on Registers_1_r10
  // Probe on Registers_1_r11
  // Probe on Registers_1_r12
  // Probe on Registers_1_r13
  // Probe on Registers_1_r14
  // Probe on Fetch_1_valc
  // Probe on Fetch_1_valp
  // Probe on Program_Counter_q
endmodule

module ALU (
  input  [63:0] aluB,
  input  [63:0] aluA,
  input  [3:0] func,
  output O,
  output Z,
  output S,
  output [63:0] valE
);

  wire adder_1_cout, or_1_out, subtractor_1_bout;
  wire [63:0] adder_1_out, and_1_out, divider_1_out, divider_1_rem, multiplier_1_cout, multiplier_1_out,
       shifter_1_out, shifter_2_out, subtractor_1_out, xor_1_out;

  Shifter #(.width(64)) shifter_1 (.in(aluB), .\dist (aluA[5:0]), .out(shifter_1_out));
  Shifter #(.shift("lr"), .width(64)) shifter_2 (.in(aluB), .\dist (aluA[5:0]), .out(shifter_2_out));
  Adder #(.width(64)) adder_1 (.a(aluB), .b(aluA), .out(adder_1_out), .cout(adder_1_cout));  // open: cin
  Subtractor #(.width(64)) subtractor_1 (
    .a(aluB), .b(aluA), .out(subtractor_1_out), .bout(subtractor_1_bout));  // open: bin
  assign and_1_out = aluB & aluA;  // AND_Gate and_1, 64 bits wide
  assign xor_1_out = aluB ^ aluA;  // XOR_Gate xor_1, 64 bits wide
  Multiplier #(.width(64)) multiplier_1 (
    .a(aluB), .b(aluA), .out(multiplier_1_out), .cout(multiplier_1_cout));  // open: cin
  Divider #(.width(64)) divider_1 (.a(aluB), .b(aluA), .out(divider_1_out), .rem(divider_1_rem));  // open: upper
  or or_1 (or_1_out, multiplier_1_cout[31], multiplier_1_cout[0], multiplier_1_cout[1], multiplier_1_cout[2], multiplier_1_cout[3], multiplier_1_cout[4], multiplier_1_cout[5], multiplier_1_cout[6], multiplier_1_cout[7], multiplier_1_cout[8], multiplier_1_cout[9], multiplier_1_cout[10], multiplier_1_cout[11], multiplier_1_cout[12], multiplier_1_cout[13], multiplier_1_cout[14], multiplier_1_cout[15], multiplier_1_cout[16], multiplier_1_cout[17], multiplier_1_cout[18], multiplier_1_cout[19], multiplier_1_cout[20], multiplier_1_cout[21], multiplier_1_cout[22], multiplier_1_cout[23], multiplier_1_cout[24], multiplier_1_cout[25], multiplier_1_cout[26], multiplier_1_cout[27], multiplier_1_cout[28], multiplier_1_cout[29], multiplier_1_cout[30], multiplier_1_cout[32], multiplier_1_cout[33], multiplier_1_cout[34], multiplier_1_cout[35], multiplier_1_cout[36], multiplier_1_cout[37], multiplier_1_cout[38], multiplier_1_cout[39], multiplier_1_cout[40], multiplier_1_cout[41], multiplier_1_cout[42], multiplier_1_cout[43], multiplier_1_cout[44], multiplier_1_cout[45], multiplier_1_cout[46], multiplier_1_cout[47], multiplier_1_cout[48], multiplier_1_cout[49], multiplier_1_cout[50], multiplier_1_cout[51], multiplier_1_cout[52], multiplier_1_cout[53], multiplier_1_cout[54], multiplier_1_cout[55], multiplier_1_cout[56], multiplier_1_cout[57], multiplier_1_cout[58], multiplier_1_cout[59], multiplier_1_cout[60], multiplier_1_cout[61], multiplier_1_cout[62], multiplier_1_cout[63]);
  Multiplexer #(.select(4), .width(64)) multiplexer_1 (
    .in0(adder_1_out), .in1(subtractor_1_out), .in2(and_1_out), .in3(xor_1_out), .in4(multiplier_1_out),
    .in5(divider_1_out), .in6(divider_1_rem), .in7(shifter_1_out), .in8(shifter_2_out), .in9({64{1'b0}}),
    .in10({64{1'b0}}), .in11({64{1'b0}}), .in12({64{1'b0}}), .in13({64{1'b0}}), .in14({64{1'b0}}),
    .in15({64{1'b0}}), .out({S, valE[62:0]}), .sel(func));
  Multiplexer #(.select(4)) multiplexer_2 (
    .in0(adder_1_cout), .in1(subtractor_1_bout), .in2(1'b0), .in3(1'b0), .in4(or_1_out), .in5(1'b0),
    .in6(1'b0), .in7(1'b0), .in8(1'b0), .in9(1'b0), .in10(1'b0), .in11(1'b0), .in12(1'b0), .in13(1'b0),
    .in14(1'b0), .in15(1'b0), .out(O), .sel(func));
  nor nor_1 (Z, valE[31], valE[0], valE[1], valE[2], valE[3], valE[4], valE[5], valE[6], valE[7], valE[8], valE[9], valE[10], valE[11], valE[12], valE[13], valE[14], valE[15], valE[16], valE[17], valE[18], valE[19], valE[20], valE[21], valE[22], valE[23], valE[24], valE[25], valE[26], valE[27], valE[28], valE[29], valE[30], valE[32], valE[33], valE[34], valE[35], valE[36], valE[37], valE[38], valE[39], valE[40], valE[41], valE[42], valE[43], valE[44], valE[45], valE[46], valE[47], valE[48], valE[49], valE[50], valE[51], valE[52], valE[53], valE[54], valE[55], valE[56], valE[57], valE[58], valE[59], valE[60], valE[61], valE[62], S);

  assign valE[63] = S;
endmodule

module SimRAM (
  input  Write,
  input  [63:0] Data_from_Memory_Stage,
  input  [63:0] Addr_from_Memory_Stage,
  input  Clock,
  input  Substep_Number,
  input  [63:0] Program_Counter,
  output Illegal_Memory_Access,
  output [63:0] First_Word,
  output [15:0] Second_Word
);

  wire and_1_out, not_1_out, not_2_out, not_3_out, or_1_out;
  wire [63:0] multiplexer_1_out;

  Multiplexer #(.width(64)) multiplexer_1 (
    .in0(Program_Counter), .in1(Addr_from_Memory_Stage), .out(multiplexer_1_out), .sel(Substep_Number));
  Illegal_Mem_Access Illegal_Mem_Access_1 (
    .Substep(Substep_Number), .Address(multiplexer_1_out), .IMA_Output(Illegal_Memory_Access));
  and and_1 (and_1_out, Write, Substep_Number);
  // Probe on multiplexer_1_out[23:0]
  not not_1 (not_1_out, and_1_out);
  or or_1 (or_1_out, Write, not_2_out);
  not not_2 (not_2_out, Substep_Number);
  not not_3 (not_3_out, Write);
  // RAM #(.addrWidth(24), .dataWidth(16), .databus("bidir"), .enables("line"), .line("octo"), .misaligned("true"), .\type ("nonvolatile")) RAM_1: pin names not known; wires that end beside it: 24'he00000, multiplexer_1_out[23:0], not_1_out, and_1_out, or_1_out, or_1_out, not_3_out, 1'b0, 1'b0, 1'b0, Clock
  assign First_Word = and_1_out ? Data_from_Memory_Stage : 64'bz;  // Controlled_Buffer controlled_buffer_1
  // also tied to VCC on the sheet: or_1_out
endmodule

module Illegal_Mem_Access (
  input  Substep,
  input  [63:0] Address,
  output IMA_Output
);

  wire and_1_out, or_1_out;

  or or_1 (or_1_out, Address[0], Address[1]);
  and and_1 (and_1_out, Substep, or_1_out);
  or or_2 (IMA_Output, and_1_out, Address[24], Address[25], Address[26], Address[27], Address[28], Address[29], Address[30], Address[31], Address[32], Address[33], Address[34], Address[35], Address[36], Address[37], Address[38], Address[39], Address[40], Address[41], Address[42], Address[43], Address[44], Address[45], Address[46], Address[47], Address[48], Address[49], Address[50], Address[51], Address[52], Address[53], Address[54], Address[55], Address[56], Address[57], Address[58], Address[59], Address[60], Address[61], Address[62], Address[63]);
endmodule

module Decode (
  input  [3:0] rA,
  input  [3:0] rB,
  input  [3:0] iCd,
  output [3:0] srcA,
  output [3:0] srcB,
  output [3:0] dstE,
  output [3:0] dstM
);

  Multiplexer #(.select(4), .width(4)) multiplexer_1 (
    .in0(4'b1111), .in1(4'b1111), .in2(rA), .in3(4'b1111), .in4(rA), .in5(4'b1111), .in6(rA), .in7(4'b1111),
    .in8(rA), .in9(rB), .in10(rA), .in11(rB), .in12(4'b1111), .in13(4'b1111), .in14(4'b1111), .in15(4'b1111),
    .out(srcA), .sel(iCd));
  Multiplexer #(.select(4), .width(4)) multiplexer_2 (
    .in0(4'b1111), .in1(4'b1111), .in2(rB), .in3(4'b1111), .in4(rB), .in5(rB), .in6(rB), .in7(rB), .in8(rB),
    .in9(rB), .in10(rB), .in11(rB), .in12(4'b1111), .in13(4'b1111), .in14(4'b1111), .in15(4'b1111),
    .out(srcB), .sel(iCd));
  Multiplexer #(.select(4), .width(4)) multiplexer_3 (
    .in0(4'b1111), .in1(4'b1111), .in2(rB), .in3(rB), .in4(4'b1111), .in5(4'b1111), .in6(rB), .in7(4'b1111),
    .in8(rB), .in9(rB), .in10(rB), .in11(rB), .in12(4'b1111), .in13(4'b1111), .in14(4'b1111), .in15(4'b1111),
    .out(dstE), .sel(iCd));
  Multiplexer #(.select(4), .width(4)) multiplexer_4 (
    .in0(4'b1111), .in1(4'b1111), .in2(4'b1111), .in3(4'b1111), .in4(4'b1111), .in5(rA), .in6(4'b1111),
    .in7(4'b1111), .in8(4'b1111), .in9(4'b1111), .in10(4'b1111), .in11(rA), .in12(4'b1111), .in13(4'b1111),
    .in14(4'b1111), .in15(4'b1111), .out(dstM), .sel(iCd));
endmodule

module Fetch (
  input  [63:0] First_Word,
  input  [15:0] Second_Word,
  input  Substep,
  input  [63:0] Program_Counter,
  input  Clock,
  output [3:0] iCd,
  output [3:0] IFn,
  output [63:0] valP,
  output [3:0] rA,
  output [3:0] rB,
  output [63:0] valC
);

  wire not_1_out;
  wire [7:0] multiplexer_1_out;
  wire [63:0] adder_1_out, multiplexer_2_out, multiplexer_3_out;

  Multiplexer #(.select(4), .width(8)) multiplexer_1 (
    .in0({8{1'b1}}), .in1({8{1'b1}}), .in2(First_Word[55:48]), .in3({4'b1111, First_Word[51:48]}),
    .in4(First_Word[55:48]), .in5(First_Word[55:48]), .in6(First_Word[55:48]), .in7({8{1'b1}}),
    .in8({4'b1111, First_Word[51:48]}), .in9({4'b1111, First_Word[51:48]}), .in10(First_Word[55:48]),
    .in11(First_Word[55:48]), .in12({8{1'b1}}), .in13({8{1'b1}}), .in14({8{1'b1}}), .in15({8{1'b1}}),
    .out(multiplexer_1_out), .sel(First_Word[63:60]));
  Multiplexer #(.select(4), .width(64)) multiplexer_2 (
    .in0({64{1'b1}}), .in1({64{1'b1}}), .in2({64{1'b1}}), .in3({First_Word[47:0], Second_Word}),
    .in4({First_Word[47:0], Second_Word}), .in5({First_Word[47:0], Second_Word}), .in6({64{1'b1}}),
    .in7({First_Word[47:0], Second_Word}), .in8({First_Word[47:0], Second_Word}), .in9({64{1'b1}}),
    .in10({64{1'b1}}), .in11({64{1'b1}}), .in12({64{1'b1}}), .in13({64{1'b1}}), .in14({64{1'b1}}),
    .in15({64{1'b1}}), .out(multiplexer_2_out), .sel(First_Word[63:60]));
  not not_1 (not_1_out, Substep);
  Register #(.width(4)) opcode (.D(First_Word[63:60]), .en(not_1_out), .clk(Clock), .Q(iCd));  // open: clr
  Register #(.width(4)) func (.D(First_Word[59:56]), .en(not_1_out), .clk(Clock), .Q(IFn));  // open: clr
  Register #(.width(4)) rA_decode (.D(multiplexer_1_out[7:4]), .en(not_1_out), .clk(Clock), .Q(rA));  // open: clr
  Register #(.width(4)) rB_decode (.D(multiplexer_1_out[3:0]), .en(not_1_out), .clk(Clock), .Q(rB));  // open: clr
  Register #(.width(64)) valC_decode (.D(multiplexer_2_out), .en(not_1_out), .clk(Clock), .Q(valC));  // open: clr
  Multiplexer #(.select(4), .width(64)) multiplexer_3 (
    .in0({64{1'b0}}), .in1(64'h1), .in2(64'h1), .in3(64'h5), .in4(64'h5), .in5(64'h5), .in6(64'h1),
    .in7(64'h5), .in8(64'h5), .in9(64'h1), .in10(64'h1), .in11(64'h1), .in12({64{1'b0}}), .in13({64{1'b0}}),
    .in14({64{1'b0}}), .in15({64{1'b0}}), .out(multiplexer_3_out), .sel(First_Word[63:60]));
  Adder #(.width(64)) adder_1 (
    .a(multiplexer_3_out), .b(Program_Counter), .out(adder_1_out), .cin(1'b0));  // open: cout
  Register #(.width(64)) nextPC (.D(adder_1_out), .en(not_1_out), .clk(Clock), .Q(valP));  // open: clr
endmodule

module Registers (
  input  [3:0] dstE,
  input  [3:0] dstM,
  input  [63:0] valE,
  input  [63:0] valM,
  input  [3:0] srcA,
  input  [3:0] srcB,
  input  Clock,
  input  Reset,
  input  Substep,
  output [63:0] eax,
  output [63:0] ecx,
  output [63:0] edx,
  output [63:0] ebx,
  output [63:0] esp,
  output [63:0] ebp,
  output [63:0] esi,
  output [63:0] edi,
  output [63:0] valA,
  output [63:0] valB,
  output [63:0] rto,
  output [63:0] r9,
  output [63:0] r10,
  output [63:0] r11,
  output [63:0] r12,
  output [63:0] r13,
  output [63:0] r14
);

  wire and_1_out, and_2_out, and_3_out, and_4_out, and_5_out, and_6_out, and_7_out, and_8_out, and_9_out,
       and_10_out, and_11_out, and_12_out, and_13_out, and_14_out, and_15_out, decoder_1_out0,
       decoder_1_out1, decoder_1_out2, decoder_1_out3, decoder_1_out4, decoder_1_out5, decoder_1_out6,
       decoder_1_out7, decoder_1_out8, decoder_1_out9, decoder_1_out10, decoder_1_out11, decoder_1_out12,
       decoder_1_out13, decoder_1_out14, decoder_1_out15, decoder_2_out0, decoder_2_out1, decoder_2_out2,
       decoder_2_out3, decoder_2_out4, decoder_2_out5, decoder_2_out6, decoder_2_out7, decoder_2_out8,
       decoder_2_out9, decoder_2_out10, decoder_2_out11, decoder_2_out12, decoder_2_out13, decoder_2_out14,
       decoder_2_out15, or_1_out, or_2_out, or_3_out, or_4_out, or_5_out, or_6_out, or_7_out, or_8_out,
       or_9_out, or_10_out, or_11_out, or_12_out, or_13_out, or_14_out, or_15_out;
  wire [63:0] multiplexer_1_out, multiplexer_2_out, multiplexer_3_out, multiplexer_4_out, multiplexer_5_out,
       multiplexer_6_out, multiplexer_7_out, multiplexer_8_out, multiplexer_9_out, multiplexer_10_out,
       multiplexer_11_out, multiplexer_12_out, multiplexer_13_out, multiplexer_14_out, multiplexer_15_out;

  Multiplexer #(.width(64)) multiplexer_1 (.in0(valM), .in1(valE), .out(multiplexer_1_out), .sel(decoder_1_out0));
  Multiplexer #(.width(64)) multiplexer_2 (.in0(valM), .in1(valE), .out(multiplexer_2_out), .sel(decoder_1_out1));
  Multiplexer #(.width(64)) multiplexer_3 (.in0(valM), .in1(valE), .out(multiplexer_3_out), .sel(decoder_1_out2));
  Multiplexer #(.width(64)) multiplexer_4 (.in0(valM), .in1(valE), .out(multiplexer_4_out), .sel(decoder_1_out3));
  Multiplexer #(.width(64)) multiplexer_5 (.in0(valM), .in1(valE), .out(multiplexer_5_out), .sel(decoder_1_out4));
  Multiplexer #(.width(64)) multiplexer_6 (.in0(valM), .in1(valE), .out(multiplexer_6_out), .sel(decoder_1_out5));
  Multiplexer #(.width(64)) multiplexer_7 (.in0(valM), .in1(valE), .out(multiplexer_7_out), .sel(decoder_1_out6));
  Multiplexer #(.width(64)) multiplexer_8 (.in0(valM), .in1(valE), .out(multiplexer_8_out), .sel(decoder_1_out7));
  Multiplexer #(.width(64)) multiplexer_9 (.in0(valM), .in1(valE), .out(multiplexer_9_out), .sel(decoder_1_out8));
  Multiplexer #(.width(64)) multiplexer_10 (.in0(valM), .in1(valE), .out(multiplexer_10_out), .sel(decoder_1_out9));
  Multiplexer #(.width(64)) multiplexer_11 (.in0(valM), .in1(valE), .out(multiplexer_11_out), .sel(decoder_1_out10));
  Multiplexer #(.width(64)) multiplexer_12 (.in0(valM), .in1(valE), .out(multiplexer_12_out), .sel(decoder_1_out11));
  Multiplexer #(.width(64)) multiplexer_13 (.in0(valM), .in1(valE), .out(multiplexer_13_out), .sel(decoder_1_out12));
  Multiplexer #(.width(64)) multiplexer_14 (.in0(valM), .in1(valE), .out(multiplexer_14_out), .sel(decoder_1_out13));
  Multiplexer #(.width(64)) multiplexer_15 (.in0(valM), .in1(valE), .out(multiplexer_15_out), .sel(decoder_1_out14));
  Decoder #(.enable("false"), .select(4)) decoder_1 (
    .out0(decoder_1_out0), .out1(decoder_1_out1), .out2(decoder_1_out2), .out3(decoder_1_out3),
    .out4(decoder_1_out4), .out5(decoder_1_out5), .out6(decoder_1_out6), .out7(decoder_1_out7),
    .out8(decoder_1_out8), .out9(decoder_1_out9), .out10(decoder_1_out10), .out11(decoder_1_out11),
    .out12(decoder_1_out12), .out13(decoder_1_out13), .out14(decoder_1_out14), .out15(decoder_1_out15),
    .sel(dstE));
  // NoConnect on decoder_1_out15
  Decoder #(.enable("false"), .select(4)) decoder_2 (
    .out0(decoder_2_out0), .out1(decoder_2_out1), .out2(decoder_2_out2), .out3(decoder_2_out3),
    .out4(decoder_2_out4), .out5(decoder_2_out5), .out6(decoder_2_out6), .out7(decoder_2_out7),
    .out8(decoder_2_out8), .out9(decoder_2_out9), .out10(decoder_2_out10), .out11(decoder_2_out11),
    .out12(decoder_2_out12), .out13(decoder_2_out13), .out14(decoder_2_out14), .out15(decoder_2_out15),
    .sel(dstM));
  // NoConnect on decoder_2_out15
  or or_1 (or_1_out, decoder_1_out0, decoder_2_out0);
  or or_2 (or_2_out, decoder_1_out1, decoder_2_out1);
  or or_3 (or_3_out, decoder_1_out2, decoder_2_out2);
  or or_4 (or_4_out, decoder_1_out3, decoder_2_out3);
  or or_5 (or_5_out, decoder_1_out4, decoder_2_out4);
  or or_6 (or_6_out, decoder_1_out5, decoder_2_out5);
  or or_7 (or_7_out, decoder_1_out6, decoder_2_out6);
  or or_8 (or_8_out, decoder_1_out7, decoder_2_out7);
  or or_9 (or_9_out, decoder_1_out8, decoder_2_out8);
  or or_10 (or_10_out, decoder_1_out9, decoder_2_out9);
  or or_11 (or_11_out, decoder_1_out10, decoder_2_out10);
  or or_12 (or_12_out, decoder_1_out11, decoder_2_out11);
  or or_13 (or_13_out, decoder_1_out12, decoder_2_out12);
  or or_14 (or_14_out, decoder_1_out13, decoder_2_out13);
  or or_15 (or_15_out, decoder_1_out14, decoder_2_out14);
  and and_1 (and_1_out, or_1_out, Substep);
  and and_2 (and_2_out, or_2_out, Substep);
  and and_3 (and_3_out, or_3_out, Substep);
  and and_4 (and_4_out, or_4_out, Substep);
  and and_5 (and_5_out, or_5_out, Substep);
  and and_6 (and_6_out, or_6_out, Substep);
  and and_7 (and_7_out, or_7_out, Substep);
  and and_8 (and_8_out, or_8_out, Substep);
  and and_9 (and_9_out, or_9_out, Substep);
  and and_10 (and_10_out, or_10_out, Substep);
  and and_11 (and_11_out, or_11_out, Substep);
  and and_12 (and_12_out, or_12_out, Substep);
  and and_13 (and_13_out, or_13_out, Substep);
  and and_14 (and_14_out, or_14_out, Substep);
  and and_15 (and_15_out, or_15_out, Substep);
  Register #(.width(64)) L_eax (.D(multiplexer_1_out), .en(and_1_out), .Q(eax), .clk(Clock), .clr(Reset));
  Register #(.width(64)) L_ecx (.D(multiplexer_2_out), .en(and_2_out), .Q(ecx), .clk(Clock), .clr(Reset));
  Register #(.width(64)) L_edx (.D(multiplexer_3_out), .en(and_3_out), .Q(edx), .clk(Clock), .clr(Reset));
  Register #(.width(64)) L_ebx (.D(multiplexer_4_out), .en(and_4_out), .Q(ebx), .clk(Clock), .clr(Reset));
  Register #(.width(64)) L_esp (.D(multiplexer_5_out), .en(and_5_out), .Q(esp), .clk(Clock), .clr(Reset));
  Register #(.width(64)) L_ebp (.D(multiplexer_6_out), .en(and_6_out), .Q(ebp), .clk(Clock), .clr(Reset));
  Register #(.width(64)) L_esi (.D(multiplexer_7_out), .en(and_7_out), .Q(esi), .clk(Clock), .clr(Reset));
  Register #(.width(64)) L_edi (.D(multiplexer_8_out), .en(and_8_out), .Q(edi), .clk(Clock), .clr(Reset));
  Register #(.width(64)) L_rto (.D(multiplexer_9_out), .en(and_9_out), .Q(rto), .clk(Clock), .clr(Reset));
  Register #(.width(64)) L_r9 (.D(multiplexer_10_out), .en(and_10_out), .Q(r9), .clk(Clock), .clr(Reset));
  Register #(.width(64)) L_r10 (.D(multiplexer_11_out), .en(and_11_out), .Q(r10), .clk(Clock), .clr(Reset));
  Register #(.width(64)) L_r11 (.D(multiplexer_12_out), .en(and_12_out), .Q(r11), .clk(Clock), .clr(Reset));
  Register #(.width(64)) L_r12 (.D(multiplexer_13_out), .en(and_13_out), .Q(r12), .clk(Clock), .clr(Reset));
  Register #(.width(64)) L_r13 (.D(multiplexer_14_out), .en(and_14_out), .Q(r13), .clk(Clock), .clr(Reset));
  Register #(.width(64)) L_r14 (.D(multiplexer_15_out), .en(and_15_out), .Q(r14), .clk(Clock), .clr(Reset));
  Multiplexer #(.select(4), .width(64)) multiplexer_16 (
    .in0(eax), .in1(ecx), .in2(edx), .in3(ebx), .in4(esp), .in5(ebp), .in6(esi), .in7(edi), .in8(rto),
    .in9(r9), .in10(r10), .in11(r11), .in12(r12), .in13(r13), .in14(r14), .in15({64{1'b0}}), .out(valA),
    .sel(srcA));
  Multiplexer #(.select(4), .width(64)) multiplexer_17 (
    .in0(eax), .in1(ecx), .in2(edx), .in3(ebx), .in4(esp), .in5(ebp), .in6(esi), .in7(edi), .in8(rto),
    .in9(r9), .in10(r10), .in11(r11), .in12(r12), .in13(r13), .in14(r14), .in15({64{1'b0}}), .out(valB),
    .sel(srcB));
endmodule

module Execute (
  input  [63:0] valA,
  input  [63:0] valB,
  input  [63:0] valC,
  input  Clock,
  input  Reset,
  input  [3:0] iCd,
  input  [3:0] iFn,
  input  Step,
  output [63:0] valE,
  output Bch
);

  wire ALU_1_o, ALU_1_s, ALU_1_z, and_1_out, Equals_1_output, multiplexer_4_out, multiplexer_5_out,
       multiplexer_6_out, O_q, S_q, Z_q;
  wire [3:0] multiplexer_3_out;
  wire [63:0] multiplexer_1_out, multiplexer_2_out;

  Multiplexer #(.select(4), .width(64)) multiplexer_1 (
    .in0({64{1'b0}}), .in1({64{1'b0}}), .in2(valA), .in3(valC), .in4(valC), .in5(valC), .in6(valA),
    .in7(valC), .in8(64'h4), .in9(64'h4), .in10(64'h4), .in11(64'h4), .in12({64{1'b0}}), .in13({64{1'b0}}),
    .in14({64{1'b0}}), .in15({64{1'b0}}), .out(multiplexer_1_out), .sel(iCd));
  Multiplexer #(.select(4), .width(64)) multiplexer_2 (
    .in0({64{1'b0}}), .in1({64{1'b0}}), .in2({64{1'b0}}), .in3({64{1'b0}}), .in4(valB), .in5(valB),
    .in6(valB), .in7({64{1'b0}}), .in8(valB), .in9(valB), .in10(valB), .in11(valB), .in12({64{1'b0}}),
    .in13({64{1'b0}}), .in14({64{1'b0}}), .in15({64{1'b0}}), .out(multiplexer_2_out), .sel(iCd));
  Multiplexer #(.select(4), .width(4)) multiplexer_3 (
    .in0(4'b0000), .in1(4'b0000), .in2(4'b0000), .in3(4'b0000), .in4(4'b0000), .in5(4'b0000), .in6(iFn),
    .in7(4'b0000), .in8(4'b0001), .in9(4'b0000), .in10(4'b0001), .in11(4'b0000), .in12(4'b0000),
    .in13(4'b0000), .in14(4'b0000), .in15(4'b0000), .out(multiplexer_3_out), .sel(iCd));
  ALU ALU_1 (
    .aluB(multiplexer_2_out), .aluA(multiplexer_1_out), .func(multiplexer_3_out), .O(ALU_1_o), .Z(ALU_1_z),
    .S(ALU_1_s), .valE(valE));
  Equals Equals_1 (.Input_1(4'b0110), .Input_2(iCd), .Output(Equals_1_output));
  Multiplexer multiplexer_4 (.in0(O_q), .in1(ALU_1_o), .out(multiplexer_4_out), .sel(and_1_out));
  Multiplexer multiplexer_5 (.in0(Z_q), .in1(ALU_1_z), .out(multiplexer_5_out), .sel(and_1_out));
  Multiplexer multiplexer_6 (.in0(S_q), .in1(ALU_1_s), .out(multiplexer_6_out), .sel(and_1_out));
  and and_1 (and_1_out, Equals_1_output, Step);
  D_Flip_Flop O (.clk(Clock), .D(multiplexer_4_out), .Q(O_q), .preset(1'b0), .reset(Reset));  // open: Qn
  D_Flip_Flop Z (.clk(Clock), .D(multiplexer_5_out), .Q(Z_q), .preset(1'b0), .reset(Reset));  // open: Qn
  D_Flip_Flop S (.clk(Clock), .D(multiplexer_6_out), .Q(S_q), .preset(1'b0), .reset(Reset));  // open: Qn
  Branch Branch_1 (.iCd(iCd), .Z(Z_q), .S(S_q), .O(O_q), .iFn(iFn), .Bch(Bch));
endmodule

// =
module Equals (
  input  [3:0] Input_1,
  input  [3:0] Input_2,
  output Output
);

  wire [3:0] xnor_1_out;

  assign xnor_1_out = ~(Input_1 ^ Input_2);  // XNOR_Gate xnor_1, 4 bits wide
  and and_1 (Output, xnor_1_out[0], xnor_1_out[1], xnor_1_out[2], xnor_1_out[3]);
endmodule

module Branch (
  input  [3:0] iCd,
  input  Z,
  input  S,
  input  O,
  input  [3:0] iFn,
  output Bch
);

  wire Equals_1_output, Equals_2_output, multiplexer_1_out, nor_1_out, not_1_out, not_2_out, not_3_out,
       or_1_out, xor_1_out;

  xor xor_1 (xor_1_out, S, O);
  or or_1 (or_1_out, Z, xor_1_out);
  Equals Equals_1 (.Input_1(4'b0111), .Input_2(iCd), .Output(Equals_1_output));
  Equals Equals_2 (.Input_1(4'b0010), .Input_2(iCd), .Output(Equals_2_output));
  not not_1 (not_1_out, Z);
  not not_2 (not_2_out, or_1_out);
  not not_3 (not_3_out, xor_1_out);
  nor nor_1 (nor_1_out, Equals_1_output, Equals_2_output);
  Multiplexer #(.select(4)) multiplexer_1 (
    .in0(1'b1), .in1(or_1_out), .in2(xor_1_out), .in3(Z), .in4(not_1_out), .in5(not_3_out), .in6(not_2_out),
    .in7(1'b1), .in8(1'b1), .in9(1'b1), .in10(1'b1), .in11(1'b1), .in12(1'b1), .in13(1'b1), .in14(1'b1),
    .in15(1'b1), .out(multiplexer_1_out), .sel(iFn));
  or or_2 (Bch, nor_1_out, multiplexer_1_out);
endmodule

module Memory (
  input  [63:0] valE,
  input  [63:0] valA,
  input  [63:0] valP,
  input  [3:0] iCd,
  output Write,
  output [63:0] Data,
  output [63:0] Address
);

  wire Equals_1_output, Equals_2_output, Equals_3_output;

  Multiplexer #(.select(4), .width(64)) multiplexer_1 (
    .in0({64{1'b0}}), .in1({64{1'b0}}), .in2({64{1'b0}}), .in3({64{1'b0}}), .in4(valE), .in5(valE),
    .in6({64{1'b0}}), .in7({64{1'b0}}), .in8(valE), .in9(valA), .in10(valE), .in11(valA), .in12({64{1'b0}}),
    .in13({64{1'b0}}), .in14({64{1'b0}}), .in15({64{1'b0}}), .out(Address), .sel(iCd));
  Multiplexer #(.select(4), .width(64)) multiplexer_2 (
    .in0({64{1'b0}}), .in1({64{1'b0}}), .in2({64{1'b0}}), .in3({64{1'b0}}), .in4(valA), .in5({64{1'b0}}),
    .in6({64{1'b0}}), .in7({64{1'b0}}), .in8(valP), .in9({64{1'b0}}), .in10(valA), .in11({64{1'b0}}),
    .in12({64{1'b0}}), .in13({64{1'b0}}), .in14({64{1'b0}}), .in15({64{1'b0}}), .out(Data), .sel(iCd));
  Equals Equals_1 (.Input_1(4'b0100), .Input_2(iCd), .Output(Equals_1_output));
  Equals Equals_2 (.Input_1(4'b1000), .Input_2(iCd), .Output(Equals_2_output));
  Equals Equals_3 (.Input_1(4'b1010), .Input_2(iCd), .Output(Equals_3_output));
  or or_1 (Write, Equals_1_output, Equals_2_output, Equals_3_output);
endmodule

module PCUpdate (
  input  [63:0] valM,
  input  [3:0] iCd,
  input  [63:0] valP,
  input  [63:0] valC,
  input  bch,
  input  Substep,
  input  Clock,
  output [63:0] nextPC
);

  wire not_1_out;
  wire [63:0] multiplexer_1_out, register_1_q;

  Multiplexer #(.width(64)) multiplexer_1 (.in0(valP), .in1(valC), .out(multiplexer_1_out), .sel(bch));
  Register #(.width(64)) register_1 (.D(valM), .en(Substep), .clk(not_1_out), .Q(register_1_q));  // open: clr
  not not_1 (not_1_out, Clock);
  Multiplexer #(.select(4), .width(64)) multiplexer_2 (
    .in0(valP), .in1(valP), .in2(valP), .in3(valP), .in4(valP), .in5(valP), .in6(valP),
    .in7(multiplexer_1_out), .in8(valC), .in9(register_1_q), .in10(valP), .in11(valP), .in12(valP),
    .in13(valP), .in14(valP), .in15(valP), .out(nextPC), .sel(iCd));
endmodule
